# Fritzing sketch alarmClock (saved by Fritzing 0.9.3b)
circuit board: 8.46667cm x 5.64444cm
breadboards: 1

parts:
  U1 = NodeMCU V3.0
  Parça1 = Adafruit DS3231 [part_number="Adafruit #3013"]
  Parça2 = Logic Level Converter
  VCC1 = 4 x AAA Battery Mount
  Röle = Keyes Relay [package=THT]

nets:
  N1: U1.D1, Parça1.SCL
  N2: U1.D2, Parça1.SDA
  3V3: U1.3V3, Parça1.Vin, Parça2.LV
  GND: U1.GND#6, U1.GND#13, U1.GND#16, U1.GND#33, Parça1.GND, Parça2.GND, VCC1.-, Röle.power
  N3: U1.D5, Parça2.TX2_LV
  N4: U1.Vin, Parça2.HV, VCC1.+, Röle.signal
  N5: Parça2.TX2_HV, Röle.ground
  N6: Röle.NC, Röle.C, Röle.NO

custom parts:
  NodeMCU V3.0: ESP8266 based NodeMCU
  Adafruit DS3231: The datasheet for the DS3231 explains that this part is an "Extremely Accurate I²C-Integrated RTC/TCXO/Crystal". And, hey, it does exactly what it says on the tin! This Real Time Clock (RTC) is the most precise you can get in a small, low power package. Most RTCs use an external 32kHz timing crystal that is used to keep time with low current draw. And that's all well and good, but those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
  Keyes Relay: The Keyes 5V relay module is suitable for SCM development, home appliance control. It uses a 5V~12V TIL control signal which can control DC / AC signal.
